# Fritzing sketch automatedFan (saved by Fritzing 0.9.3b)
breadboards: 2

parts:
  S1 = Pushbutton [package="[THT]"]
  S2 = Pushbutton [package="[THT]"]
  S3 = Pushbutton [package="[THT]"]
  hc-sr1 = hc-sr04
  M1 = DC Motor
  VCC1 = Battery block 9V
  Part1 = Thumb Joystick
  Part2 = Arduino Uno (Rev3) - ICSP
  LCD1 = LCD screen
  J1 = Basic Servo
  R1 = Resistor [tolerance=±5% resistance=330 package=THT]
  R2 = Resistor [tolerance=±5% resistance=10 package="0402 [SMD]"]
  Q1 = NPN-Transistor [package="SOT-23 [SMD]"]
  R3 = Resistor [tolerance=±5% resistance=330 package="1206 [SMD]"]
  D1 = Rectifier Diode [part_number=1N4001 package="300 mil [THT]"]
  R4 = Resistor [tolerance=±5% resistance=10 package="0402 [SMD]"]
  R5 = Resistor [tolerance=±5% resistance=10 package="0402 [SMD]"]
  R6 = Resistor [tolerance=±5% resistance=10 package="0402 [SMD]"]

nets:
  VCC: S1.Pin_1, S1.Pin_2, S2.Pin_1, S2.Pin_2, S3.Pin_1, S3.Pin_2, hc-sr1.VCC, hc-sr1.Trig, Part1.VCC, Part2.A0, LCD1.VDD, J1.vcc
  N1: S1.Pin_3, S1.Pin_4, Part2.D8, R5.Pin_1
  N2: S2.Pin_3, S2.Pin_4, Part2.D7, R6.Pin_0
  N3: S3.Pin_3, S3.Pin_4, Part2.D10_PWM/SS, R4.Pin_0
  N4: hc-sr1.Echo, Part2.A1
  GND: hc-sr1.GND, VCC1.-, Part1.GND, LCD1.VSS, LCD1.R/W, LCD1.LED-, R1.Pin_0, R2.Pin_1, Q1.1, R4.Pin_1, R5.Pin_0, R6.Pin_1
  N5: M1.pin_1, Q1.2, D1.anode
  N6: M1.pin_2, VCC1.+, D1.cathode
  N7: Part1.SEL, Part2.D13/SCK
  N8: Part1.VERT, Part2.A4/SDA
  N9: Part2.ICSP_MISO, Part2.D12/MISO, LCD1.RS
  N10: Part2.D11_PWM/MOSI, LCD1.E
  N11: Part2.D2, LCD1.DB7
  N12: Part2.D3_PWM, R3.Pin_0
  N13: Part2.D4, LCD1.DB6
  N14: Part2.D5_PWM, LCD1.DB5
  N15: Part2.D6_PWM, LCD1.DB4
  N16: LCD1.V0, R1.Pin_1
  N17: LCD1.LED+, R2.Pin_0
  N18: Q1.0, R3.Pin_1
